# Fritzing sketch output_gpio (saved by Fritzing 1.0.2b)
breadboards: 1

parts:
  U3 = Atmega32_16_pu [package=dil40-6-zif_socket]
  LED1 = LED - 5mm [color="Green (560nm)" current=0.030A package="5 mm [THT]"]
  LED2 = LED - 5mm [color="Red (633nm)" current=0.030A package="5 mm [THT]"]
  R1 = Resistor [tolerance=±5% power=0.25W resistance=220 package=THT]
  R2 = Resistor [tolerance=±5% power=0.25W resistance=220 package=THT]
  VCC2 = 4 x AAA Battery Mount
  S1 = Pushbutton [package="[THT]"]

nets:
  N1: U3.P$3, R2.Pin_0
  N2: U3.P$4, R1.Pin_0
  N3: U3.P$10, VCC2.+
  N4: U3.P$11, LED1.cathode, LED2.cathode, VCC2.-, S1.Pin_3, S1.Pin_4
  N5: U3.P$29, S1.Pin_1, S1.Pin_2
  N6: LED1.anode, R1.Pin_1
  N7: LED2.anode, R2.Pin_1

custom parts:
  Atmega32_16_pu: Lever-action ZIF socket for 40-pin ICs
