# Fritzing sketch timer_basic-ctc (saved by Fritzing 1.0.2b)
breadboards: 1

parts:
  R4 = Resistor [tolerance=±5% power=0.25W resistance=220 package=THT]
  LED3 = LED - 5mm [color="Green (555nm)" current=0.030A package="5 mm [THT]"]
  U1 = Atmega32_16_pu [package=dil40-6-zif_socket]
  VCC1 = 4 x AAA Battery Mount

nets:
  N1: R4.Pin_0, U1.P$11, VCC1.-
  N2: R4.Pin_1, LED3.cathode
  N3: LED3.anode, U1.P$1
  N4: U1.P$10, VCC1.+

custom parts:
  Atmega32_16_pu: Lever-action ZIF socket for 40-pin ICs
