# Fritzing sketch usart_interrupt (saved by Fritzing 1.0.2b)
breadboards: 1

parts:
  USB_UART3 = USB-TTL UART
  R4 = Resistor [tolerance=±5% power=0.25W resistance=220 package=THT]
  LED3 = LED - 5mm [color="Yellow (595nm)" current=0.030A package="5 mm [THT]"]
  U1 = Atmega32_16_pu [package=dil40-6-zif_socket]

nets:
  N1: USB_UART3.pin5, R4.Pin_0, U1.P$11
  N2: USB_UART3.pin6, U1.P$15
  N3: USB_UART3.pin7, U1.P$14
  N4: USB_UART3.pin9, U1.P$10
  N5: R4.Pin_1, LED3.cathode
  N6: LED3.anode, U1.P$22

custom parts:
  USB-TTL UART: USB programmer interface incorporating Silicon Labs CP2102 UART
  Atmega32_16_pu: Lever-action ZIF socket for 40-pin ICs
